# Fritzing sketch 3ButtonResistorLadder (saved by Fritzing 0.9.2b)
breadboards: 1

parts:
  S3 = Momentary Switch [package=ksa_sealed_tac_switch]
  S4 = Momentary Switch [package=ksa_sealed_tac_switch]
  S5 = Momentary Switch [package=ksa_sealed_tac_switch]
  R1 = Resistor [tolerance=±5% resistance=10k package=THT]
  R2 = Resistor [tolerance=±5% resistance=10k package=THT]
  R3 = Resistor [tolerance=±5% resistance=10k package=THT]
  R4 = Resistor [tolerance=±5% resistance=10k package=THT]
  R5 = Resistor [tolerance=±5% resistance=10k package=THT]
  Part1 = Arduino Uno (Rev3)

nets:
  N1: S3.2, S4.2, S5.2, R5.Pin_0, Part1.A0
  N2: S3.3, R1.Pin_1, R2.Pin_0
  N3: S4.3, R2.Pin_1, R3.Pin_0
  N4: S5.3, R3.Pin_1, R4.Pin_0
  N5: R1.Pin_0, Part1.5V
  N6: R4.Pin_1, R5.Pin_1, Part1.GND
